// Logisim project CTRL.circ as structural Verilog: 4 circuits, main circuit main
module main (
  input  [7:0] ir
);

  wire clock_1_out, controlled_buffer_1_out, dec_1_hlt, dec_1_nop, nop_1_clr;
  wire [7:0] register_1_q;
  wire [15:0] ring_t;

  Register register_1 (.D(ir), .en(1'b1), .Q(register_1_q), .clr(1'b0));  // open: clk
  Clock clock_1 (.out(clock_1_out));
  assign controlled_buffer_1_out = dec_1_hlt ? clock_1_out : 1'bz;  // Controlled_Buffer controlled_buffer_1
  Hex_Digit_Display #(.decimalPoint("false")) irrr (.value(register_1_q[7:4]));
  Hex_Digit_Display #(.decimalPoint("false")) irr (.value(register_1_q[3:0]));
  Tring ring (.CLK(controlled_buffer_1_out), .CLR(nop_1_clr), .T(ring_t));
  dec dec_1 (
    .IR(register_1_q), .NOP(dec_1_nop), .HLT(dec_1_hlt));  // open: CLX, CLY, CLA, OUX, OUY, OUA, CMX, CMY, CMA, CMV, CALL, STX, STY, STA, JZ, JNZ, JN, JL, JG, JE, RET, ADX, ADY, ADA, ADI, ADV, SUX, SUY, SUA, SUI, SUV, LDX, LDY, LDA, LDXI, LDYI, LDAI, MXY, MXA, MYX, MYA, MAX, MAY, ANX, ANY, ANA, ANV, ORX, ORY, ORA, ORV, XOX, XOY, XOA, XOV, NOX, NOY, NOA, NOV
  NOP nop_1 (.T13(ring_t[13]), .I_NOP(dec_1_nop), .CLR(nop_1_clr));
endmodule

module Tring (
  input  CLK,
  input  CLR,
  output [15:0] T
);

  wire j_k_ff_1_q, j_k_ff_2_qn, j_k_ff_3_qn, j_k_ff_4_qn, j_k_ff_5_qn, j_k_ff_6_qn, j_k_ff_7_qn, j_k_ff_8_qn,
       j_k_ff_9_qn, j_k_ff_10_qn, j_k_ff_11_qn, j_k_ff_12_qn, j_k_ff_13_qn, j_k_ff_14_qn, j_k_ff_15_qn,
       j_k_ff_16_qn;

  J_K_Flip_Flop j_k_ff_1 (
    .J(j_k_ff_16_qn), .K(T[15]), .clk(CLK), .Q(j_k_ff_1_q), .Qn(T[0]), .preset(1'b0), .reset(CLR));
  J_K_Flip_Flop j_k_ff_2 (.J(T[0]), .K(j_k_ff_1_q), .clk(CLK), .Q(T[1]), .Qn(j_k_ff_2_qn), .preset(1'b0), .reset(CLR));
  J_K_Flip_Flop j_k_ff_3 (.J(T[1]), .K(j_k_ff_2_qn), .clk(CLK), .Q(T[2]), .Qn(j_k_ff_3_qn), .preset(1'b0), .reset(CLR));
  J_K_Flip_Flop j_k_ff_4 (.J(T[2]), .K(j_k_ff_3_qn), .clk(CLK), .Q(T[3]), .Qn(j_k_ff_4_qn), .preset(1'b0), .reset(CLR));
  J_K_Flip_Flop j_k_ff_5 (.J(T[3]), .K(j_k_ff_4_qn), .clk(CLK), .Q(T[4]), .Qn(j_k_ff_5_qn), .preset(1'b0), .reset(CLR));
  J_K_Flip_Flop j_k_ff_6 (.J(T[4]), .K(j_k_ff_5_qn), .clk(CLK), .Q(T[5]), .Qn(j_k_ff_6_qn), .preset(1'b0), .reset(CLR));
  J_K_Flip_Flop j_k_ff_7 (.J(T[5]), .K(j_k_ff_6_qn), .clk(CLK), .Q(T[6]), .Qn(j_k_ff_7_qn), .preset(1'b0), .reset(CLR));
  J_K_Flip_Flop j_k_ff_8 (.J(T[6]), .K(j_k_ff_7_qn), .clk(CLK), .Q(T[7]), .Qn(j_k_ff_8_qn), .preset(1'b0), .reset(CLR));
  J_K_Flip_Flop j_k_ff_9 (.J(T[7]), .K(j_k_ff_8_qn), .clk(CLK), .Q(T[8]), .Qn(j_k_ff_9_qn), .preset(1'b0), .reset(CLR));
  J_K_Flip_Flop j_k_ff_10 (
    .J(T[8]), .K(j_k_ff_9_qn), .clk(CLK), .Q(T[9]), .Qn(j_k_ff_10_qn), .preset(1'b0), .reset(CLR));
  J_K_Flip_Flop j_k_ff_11 (
    .J(T[9]), .K(j_k_ff_10_qn), .clk(CLK), .Q(T[10]), .Qn(j_k_ff_11_qn), .preset(1'b0), .reset(CLR));
  J_K_Flip_Flop j_k_ff_12 (
    .J(T[10]), .K(j_k_ff_11_qn), .clk(CLK), .Q(T[11]), .Qn(j_k_ff_12_qn), .preset(1'b0), .reset(CLR));
  J_K_Flip_Flop j_k_ff_13 (
    .J(T[11]), .K(j_k_ff_12_qn), .clk(CLK), .Q(T[12]), .Qn(j_k_ff_13_qn), .preset(1'b0), .reset(CLR));
  J_K_Flip_Flop j_k_ff_14 (
    .J(T[12]), .K(j_k_ff_13_qn), .clk(CLK), .Q(T[13]), .Qn(j_k_ff_14_qn), .preset(1'b0), .reset(CLR));
  J_K_Flip_Flop j_k_ff_15 (
    .J(T[13]), .K(j_k_ff_14_qn), .clk(CLK), .Q(T[14]), .Qn(j_k_ff_15_qn), .preset(1'b0), .reset(CLR));
  J_K_Flip_Flop j_k_ff_16 (
    .J(T[14]), .K(j_k_ff_15_qn), .clk(CLK), .Q(T[15]), .Qn(j_k_ff_16_qn), .preset(1'b0), .reset(CLR));
endmodule

module dec (
  input  [7:0] IR,
  output NOP,
  output CLX,
  output CLY,
  output CLA,
  output OUX,
  output OUY,
  output OUA,
  output CMX,
  output CMY,
  output CMA,
  output CMV,
  output CALL,
  output STX,
  output STY,
  output STA,
  output JZ,
  output JNZ,
  output JN,
  output JL,
  output JG,
  output JE,
  output RET,
  output HLT,
  output ADX,
  output ADY,
  output ADA,
  output ADI,
  output ADV,
  output SUX,
  output SUY,
  output SUA,
  output SUI,
  output SUV,
  output LDX,
  output LDY,
  output LDA,
  output LDXI,
  output LDYI,
  output LDAI,
  output MXY,
  output MXA,
  output MYX,
  output MYA,
  output MAX,
  output MAY,
  output ANX,
  output ANY,
  output ANA,
  output ANV,
  output ORX,
  output ORY,
  output ORA,
  output ORV,
  output XOX,
  output XOY,
  output XOA,
  output XOV,
  output NOX,
  output NOY,
  output NOA,
  output NOV
);

  wire decoder_1_out0, decoder_1_out1, decoder_1_out2, decoder_1_out3, decoder_1_out4, decoder_1_out5,
       decoder_1_out6, decoder_1_out7, decoder_2_out0, decoder_2_out1, decoder_2_out2, decoder_2_out3,
       decoder_2_out4, decoder_2_out5, decoder_2_out6, decoder_3_out0, decoder_3_out1, decoder_3_out2,
       decoder_3_out3, decoder_3_out4, decoder_3_out5, decoder_3_out6, decoder_3_out7, decoder_4_out0,
       decoder_4_out1, decoder_4_out2, decoder_4_out3, decoder_4_out4, decoder_4_out5, decoder_4_out6,
       decoder_4_out7, decoder_5_out0, decoder_5_out1, decoder_5_out2, decoder_5_out3, decoder_5_out4,
       decoder_6_out0, decoder_6_out1, decoder_6_out2, decoder_6_out3, decoder_6_out4, decoder_7_out0,
       decoder_7_out1, decoder_7_out2, decoder_7_out3, decoder_7_out4, decoder_7_out5, decoder_8_out0,
       decoder_8_out1, decoder_8_out2, decoder_8_out3, decoder_8_out4, decoder_8_out5, decoder_9_out0,
       decoder_9_out1, decoder_9_out2, decoder_9_out3, decoder_9_out4, decoder_9_out5, decoder_9_out6,
       decoder_9_out7, decoder_10_out0, decoder_10_out1, decoder_10_out2, decoder_10_out3, decoder_10_out4,
       decoder_10_out5, decoder_10_out6, decoder_10_out7;

  Decoder #(.select(3)) decoder_1 (
    .out0(decoder_1_out0), .out1(decoder_1_out1), .out2(decoder_1_out2), .out3(decoder_1_out3),
    .out4(decoder_1_out4), .out5(decoder_1_out5), .out6(decoder_1_out6), .out7(decoder_1_out7),
    .sel(IR[5:3]), .en(IR[6]));
  Decoder #(.select(3)) decoder_2 (
    .out0(decoder_2_out0), .out1(decoder_2_out1), .out2(decoder_2_out2), .out3(decoder_2_out3),
    .out4(decoder_2_out4), .out5(decoder_2_out5), .out6(decoder_2_out6), .sel(IR[2:0]), .en(decoder_1_out0));  // open: out7
  Decoder #(.select(3)) decoder_3 (
    .out0(decoder_3_out0), .out1(decoder_3_out1), .out2(decoder_3_out2), .out3(decoder_3_out3),
    .out4(decoder_3_out4), .out5(decoder_3_out5), .out6(decoder_3_out6), .out7(decoder_3_out7),
    .sel(IR[2:0]), .en(decoder_1_out1));
  Decoder #(.select(3)) decoder_4 (
    .out0(decoder_4_out0), .out1(decoder_4_out1), .out2(decoder_4_out2), .out3(decoder_4_out3),
    .out4(decoder_4_out4), .out5(decoder_4_out5), .out6(decoder_4_out6), .out7(decoder_4_out7),
    .sel(IR[2:0]), .en(decoder_1_out2));
  Decoder #(.select(3)) decoder_5 (
    .out0(decoder_5_out0), .out1(decoder_5_out1), .out2(decoder_5_out2), .out3(decoder_5_out3),
    .out4(decoder_5_out4), .sel(IR[2:0]), .en(decoder_1_out3));  // open: out5, out6, out7
  Decoder #(.select(3)) decoder_6 (
    .out0(decoder_6_out0), .out1(decoder_6_out1), .out2(decoder_6_out2), .out3(decoder_6_out3),
    .out4(decoder_6_out4), .sel(IR[2:0]), .en(decoder_1_out4));  // open: out5, out6, out7
  Decoder #(.select(3)) decoder_7 (
    .out0(decoder_7_out0), .out1(decoder_7_out1), .out2(decoder_7_out2), .out3(decoder_7_out3),
    .out4(decoder_7_out4), .out5(decoder_7_out5), .sel(IR[2:0]), .en(decoder_1_out5));  // open: out6, out7
  Decoder #(.select(3)) decoder_8 (
    .out0(decoder_8_out0), .out1(decoder_8_out1), .out2(decoder_8_out2), .out3(decoder_8_out3),
    .out4(decoder_8_out4), .out5(decoder_8_out5), .sel(IR[2:0]), .en(decoder_1_out6));  // open: out6, out7
  Decoder #(.select(3)) decoder_9 (
    .out0(decoder_9_out0), .out1(decoder_9_out1), .out2(decoder_9_out2), .out3(decoder_9_out3),
    .out4(decoder_9_out4), .out5(decoder_9_out5), .out6(decoder_9_out6), .out7(decoder_9_out7),
    .sel(IR[2:0]), .en(decoder_1_out7));
  Decoder #(.select(3)) decoder_10 (
    .out0(decoder_10_out0), .out1(decoder_10_out1), .out2(decoder_10_out2), .out3(decoder_10_out3),
    .out4(decoder_10_out4), .out5(decoder_10_out5), .out6(decoder_10_out6), .out7(decoder_10_out7),
    .sel(IR[2:0]), .en(IR[7]));
  not not_1 (NOP, decoder_2_out0);
  not not_2 (CLY, decoder_2_out2);
  not not_3 (OUX, decoder_2_out4);
  not not_4 (OUA, decoder_2_out6);
  not not_5 (CMX, decoder_3_out0);
  not not_6 (CMA, decoder_3_out2);
  not not_7 (CALL, decoder_3_out4);
  not not_8 (STY, decoder_3_out6);
  not not_9 (JZ, decoder_4_out0);
  not not_10 (JN, decoder_4_out2);
  not not_11 (JG, decoder_4_out4);
  not not_12 (RET, decoder_4_out6);
  not not_13 (ADX, decoder_5_out0);
  not not_14 (ADA, decoder_5_out2);
  not not_15 (ADV, decoder_5_out4);
  not not_16 (SUX, decoder_6_out0);
  not not_17 (SUA, decoder_6_out2);
  not not_18 (SUV, decoder_6_out4);
  not not_19 (LDX, decoder_7_out0);
  not not_20 (LDA, decoder_7_out2);
  not not_21 (LDYI, decoder_7_out4);
  not not_22 (MXY, decoder_8_out0);
  not not_23 (MYX, decoder_8_out2);
  not not_24 (MAX, decoder_8_out4);
  not not_25 (ANX, decoder_9_out0);
  not not_26 (ANA, decoder_9_out2);
  not not_27 (ORX, decoder_9_out4);
  not not_28 (ORA, decoder_9_out6);
  not not_29 (XOX, decoder_10_out0);
  not not_30 (XOA, decoder_10_out2);
  not not_31 (NOX, decoder_10_out4);
  not not_32 (NOA, decoder_10_out6);
  not not_33 (CLX, decoder_2_out1);
  not not_34 (CLA, decoder_2_out3);
  not not_35 (OUY, decoder_2_out5);
  not not_36 (CMY, decoder_3_out1);
  not not_37 (CMV, decoder_3_out3);
  not not_38 (STX, decoder_3_out5);
  not not_39 (STA, decoder_3_out7);
  not not_40 (JNZ, decoder_4_out1);
  not not_41 (JL, decoder_4_out3);
  not not_42 (JE, decoder_4_out5);
  not not_43 (HLT, decoder_4_out7);
  not not_44 (ADY, decoder_5_out1);
  not not_45 (ADI, decoder_5_out3);
  not not_46 (SUY, decoder_6_out1);
  not not_47 (SUI, decoder_6_out3);
  not not_48 (LDY, decoder_7_out1);
  not not_49 (LDXI, decoder_7_out3);
  not not_50 (LDAI, decoder_7_out5);
  not not_51 (MXA, decoder_8_out1);
  not not_52 (MYA, decoder_8_out3);
  not not_53 (MAY, decoder_8_out5);
  not not_54 (ANY, decoder_9_out1);
  not not_55 (ANV, decoder_9_out3);
  not not_56 (ORY, decoder_9_out5);
  not not_57 (ORV, decoder_9_out7);
  not not_58 (XOY, decoder_10_out1);
  not not_59 (XOV, decoder_10_out3);
  not not_60 (NOY, decoder_10_out5);
  not not_61 (NOV, decoder_10_out7);
endmodule

module NOP (
  input  T13,
  input  I_NOP,
  output CLR
);

  and and_1 (CLR, T13, I_NOP);
endmodule
