// Logisim project Control.circ as structural Verilog: 2 circuits, main circuit main
module main (
  output INC,
  output ENpcLDm,
  output ENramLDir,
  output ENir
);

  wire clock_1_out, dipswitch_1_sw1, dipswitch_1_sw2, dipswitch_1_sw3, dipswitch_1_sw4, dipswitch_1_sw5,
       dipswitch_1_sw6, dipswitch_1_sw7, dipswitch_1_sw8, not_9_out, or_1_out, or_2_out, TRing_t3, TRing_t9;

  DipSwitch dipswitch_1 (
    .sw1(dipswitch_1_sw1), .sw2(dipswitch_1_sw2), .sw3(dipswitch_1_sw3), .sw4(dipswitch_1_sw4),
    .sw5(dipswitch_1_sw5), .sw6(dipswitch_1_sw6), .sw7(dipswitch_1_sw7), .sw8(dipswitch_1_sw8));
  Clock clock_1 (.out(clock_1_out));
  // NOT_Gate not_1 has open pins: in=dipswitch_1_sw1, out=open
  // NOT_Gate not_2 has open pins: in=dipswitch_1_sw2, out=open
  // NOT_Gate not_3 has open pins: in=dipswitch_1_sw3, out=open
  // NOT_Gate not_4 has open pins: in=dipswitch_1_sw4, out=open
  // NOT_Gate not_5 has open pins: in=dipswitch_1_sw5, out=open
  // NOT_Gate not_6 has open pins: in=dipswitch_1_sw6, out=open
  // NOT_Gate not_7 has open pins: in=dipswitch_1_sw7, out=open
  // NOT_Gate not_8 has open pins: in=dipswitch_1_sw8, out=open
  not not_9 (not_9_out, or_1_out);
  or or_1 (or_1_out, TRing_t3, ENir);
  not not_10 (ENir, or_2_out);
  or or_2 (or_2_out, not_9_out, TRing_t9);
  ring TRing (
    .CLK(clock_1_out), .T0(INC), .T1(ENpcLDm), .T2(ENramLDir), .T3(TRing_t3), .T9(TRing_t9));  // open: CLR, T4, T5, T6, T7, T8
  // AND_Gate and_1 is placed but not wired
endmodule

module ring (
  input  CLK,
  input  CLR,
  output T0,
  output T1,
  output T2,
  output T5,
  output T3,
  output T4,
  output T6,
  output T7,
  output T8,
  output T9
);

  wire j_k_ff_1_q, j_k_ff_2_qn, j_k_ff_3_qn, j_k_ff_4_qn, j_k_ff_5_qn, j_k_ff_6_qn, j_k_ff_7_qn, j_k_ff_8_qn,
       j_k_ff_9_qn, j_k_ff_10_qn;

  J_K_Flip_Flop j_k_ff_1 (.J(j_k_ff_10_qn), .K(T9), .clk(CLK), .Q(j_k_ff_1_q), .Qn(T0), .preset(1'b0), .reset(CLR));
  J_K_Flip_Flop j_k_ff_2 (.J(T0), .K(j_k_ff_1_q), .clk(CLK), .Q(T1), .Qn(j_k_ff_2_qn), .preset(1'b0), .reset(CLR));
  J_K_Flip_Flop j_k_ff_3 (.J(T1), .K(j_k_ff_2_qn), .clk(CLK), .Q(T2), .Qn(j_k_ff_3_qn), .preset(1'b0), .reset(CLR));
  J_K_Flip_Flop j_k_ff_4 (.J(T2), .K(j_k_ff_3_qn), .clk(CLK), .Q(T3), .Qn(j_k_ff_4_qn), .preset(1'b0), .reset(CLR));
  J_K_Flip_Flop j_k_ff_5 (.J(T3), .K(j_k_ff_4_qn), .clk(CLK), .Q(T4), .Qn(j_k_ff_5_qn), .preset(1'b0), .reset(CLR));
  J_K_Flip_Flop j_k_ff_6 (.J(T4), .K(j_k_ff_5_qn), .clk(CLK), .Q(T5), .Qn(j_k_ff_6_qn), .preset(1'b0), .reset(CLR));
  J_K_Flip_Flop j_k_ff_7 (.J(T5), .K(j_k_ff_6_qn), .clk(CLK), .Q(T6), .Qn(j_k_ff_7_qn), .preset(1'b0), .reset(CLR));
  J_K_Flip_Flop j_k_ff_8 (.J(T6), .K(j_k_ff_7_qn), .clk(CLK), .Q(T7), .Qn(j_k_ff_8_qn), .preset(1'b0), .reset(CLR));
  J_K_Flip_Flop j_k_ff_9 (.J(T7), .K(j_k_ff_8_qn), .clk(CLK), .Q(T8), .Qn(j_k_ff_9_qn), .preset(1'b0), .reset(CLR));
  J_K_Flip_Flop j_k_ff_10 (.J(T8), .K(j_k_ff_9_qn), .clk(CLK), .Q(T9), .Qn(j_k_ff_10_qn), .preset(1'b0), .reset(CLR));
endmodule
