// Logisim project sim.circ as structural Verilog
module PC (
  input  CLR,
  input  CLK,
  input  INP,
  input  [7:0] W,
  input  LDP1,
  input  LDP,
  input  LDP2,
  output [7:0] PCL,
  output [7:0] PCH
);

  wire and_1_out, or_1_out;
  wire [7:0] register_1_q, register_2_q;

  and and_1 (and_1_out, LDP, CLK);
  Register register_1 (.D(W), .en(LDP1), .clk(CLK), .Q(register_1_q), .clr(CLR));
  or or_1 (or_1_out, and_1_out, PCL[7]);
  Register register_2 (.D(W), .en(LDP2), .clk(CLK), .Q(register_2_q), .clr(CLR));
  Counter #(.trigger("falling")) counter_1 (
    .clr(CLR), .load(LDP), .up(1'b1), .count(1'b1), .clk(INP), .D(register_1_q), .Q(PCL));  // open: carry
  Counter #(.trigger("falling")) counter_2 (
    .clr(CLR), .load(LDP), .up(1'b1), .count(1'b1), .clk(or_1_out), .D(register_2_q), .Q(PCH));  // open: carry
endmodule

module RING (
  input  CLK,
  input  CLR,
  output [17:0] T
);

  wire j_k_ff_1_q, j_k_ff_2_qn, j_k_ff_3_qn, j_k_ff_4_qn, j_k_ff_5_qn, j_k_ff_6_qn, j_k_ff_7_qn, j_k_ff_8_qn,
       j_k_ff_9_qn, j_k_ff_10_qn, j_k_ff_11_qn, j_k_ff_12_qn, j_k_ff_13_qn, j_k_ff_14_qn, j_k_ff_15_qn,
       j_k_ff_16_qn, j_k_ff_17_qn, j_k_ff_18_qn;

  J_K_Flip_Flop j_k_ff_1 (
    .J(j_k_ff_18_qn), .K(T[17]), .clk(CLK), .Q(j_k_ff_1_q), .Qn(T[0]), .preset(1'b0), .reset(CLR));
  J_K_Flip_Flop j_k_ff_2 (.J(T[0]), .K(j_k_ff_1_q), .clk(CLK), .Q(T[1]), .Qn(j_k_ff_2_qn), .preset(1'b0), .reset(CLR));
  J_K_Flip_Flop j_k_ff_3 (.J(T[1]), .K(j_k_ff_2_qn), .clk(CLK), .Q(T[2]), .Qn(j_k_ff_3_qn), .preset(1'b0), .reset(CLR));
  J_K_Flip_Flop j_k_ff_4 (.J(T[2]), .K(j_k_ff_3_qn), .clk(CLK), .Q(T[3]), .Qn(j_k_ff_4_qn), .preset(1'b0), .reset(CLR));
  J_K_Flip_Flop j_k_ff_5 (.J(T[3]), .K(j_k_ff_4_qn), .clk(CLK), .Q(T[4]), .Qn(j_k_ff_5_qn), .preset(1'b0), .reset(CLR));
  J_K_Flip_Flop j_k_ff_6 (.J(T[4]), .K(j_k_ff_5_qn), .clk(CLK), .Q(T[5]), .Qn(j_k_ff_6_qn), .preset(1'b0), .reset(CLR));
  J_K_Flip_Flop j_k_ff_7 (.J(T[5]), .K(j_k_ff_6_qn), .clk(CLK), .Q(T[6]), .Qn(j_k_ff_7_qn), .preset(1'b0), .reset(CLR));
  J_K_Flip_Flop j_k_ff_8 (.J(T[6]), .K(j_k_ff_7_qn), .clk(CLK), .Q(T[7]), .Qn(j_k_ff_8_qn), .preset(1'b0), .reset(CLR));
  J_K_Flip_Flop j_k_ff_9 (.J(T[7]), .K(j_k_ff_8_qn), .clk(CLK), .Q(T[8]), .Qn(j_k_ff_9_qn), .preset(1'b0), .reset(CLR));
  J_K_Flip_Flop j_k_ff_10 (
    .J(T[8]), .K(j_k_ff_9_qn), .clk(CLK), .Q(T[9]), .Qn(j_k_ff_10_qn), .preset(1'b0), .reset(CLR));
  J_K_Flip_Flop j_k_ff_11 (
    .J(T[9]), .K(j_k_ff_10_qn), .clk(CLK), .Q(T[10]), .Qn(j_k_ff_11_qn), .preset(1'b0), .reset(CLR));
  J_K_Flip_Flop j_k_ff_12 (
    .J(T[10]), .K(j_k_ff_11_qn), .clk(CLK), .Q(T[11]), .Qn(j_k_ff_12_qn), .preset(1'b0), .reset(CLR));
  J_K_Flip_Flop j_k_ff_13 (
    .J(T[11]), .K(j_k_ff_12_qn), .clk(CLK), .Q(T[12]), .Qn(j_k_ff_13_qn), .preset(1'b0), .reset(CLR));
  J_K_Flip_Flop j_k_ff_14 (
    .J(T[12]), .K(j_k_ff_13_qn), .clk(CLK), .Q(T[13]), .Qn(j_k_ff_14_qn), .preset(1'b0), .reset(CLR));
  J_K_Flip_Flop j_k_ff_15 (
    .J(T[13]), .K(j_k_ff_14_qn), .clk(CLK), .Q(T[14]), .Qn(j_k_ff_15_qn), .preset(1'b0), .reset(CLR));
  J_K_Flip_Flop j_k_ff_16 (
    .J(T[14]), .K(j_k_ff_15_qn), .clk(CLK), .Q(T[15]), .Qn(j_k_ff_16_qn), .preset(1'b0), .reset(CLR));
  J_K_Flip_Flop j_k_ff_17 (
    .J(T[15]), .K(j_k_ff_16_qn), .clk(CLK), .Q(T[16]), .Qn(j_k_ff_17_qn), .preset(1'b0), .reset(CLR));
  J_K_Flip_Flop j_k_ff_18 (
    .J(T[16]), .K(j_k_ff_17_qn), .clk(CLK), .Q(T[17]), .Qn(j_k_ff_18_qn), .preset(1'b0), .reset(CLR));
endmodule
